# Fritzing sketch Skematik 1 LED + 1 TOMBOL (saved by Fritzing 0.9.2b)
breadboards: 1

parts:
  Part1 = Arduino Uno (Rev3)
  LED1 = LED - 5mm [color="Red (633nm)" package="5 mm [THT]"]
  S1 = Pushbutton [package="[SMD]"]
  R2 = Resistor [tolerance=±5% resistance=1k package="0805 [SMD]"]
  R1 = Resistor [tolerance=±5% resistance=220 package="0603 [SMD]"]

nets:
  N1: Part1.D13/SCK, R1.Pin_1
  N2: Part1.D7, S1.Pin_1, S1.Pin_2, R2.Pin_0
  N3: Part1.5V, S1.Pin_3, S1.Pin_4
  N4: Part1.GND, LED1.cathode, R2.Pin_1
  N5: LED1.anode, R1.Pin_0

notes:
  Resistor 220Ω untuk Lampu LED
  Resistor 1kΩ untuk Tombol Push

// code stored in the sketch: 1 LED + 1 TOMBOL.ino
const int pinLED = 8; //  nomor pin LED
const int pinTombol = 2; // nomor pin Tombol


bool statusTombolAkhir = LOW;  // status Tombol terakhir
bool statusLED = LOW;         // status LED


void setup() {
  pinMode(pinLED, OUTPUT);    // LED sebagai output
  pinMode(pinTombol, INPUT);  // Tombol sebagai input
}


void loop() {
  bool statusTombol = digitalRead(pinTombol);  // cek status Tombol
  if (statusTombol != statusTombolAkhir) {       // jika status Tombol berubah dari sebelumnya
    if (statusTombol == HIGH) {                  // jika Tombol berubah ke status LOW (dilepas)
      if (statusLED == LOW) {          // jika status LED hidup
        digitalWrite(pinLED, HIGH); // maka LED dimatikan
        statusLED = HIGH;
      } else {                        // jika status LED mati
        digitalWrite(pinLED, LOW);  // maka LED dihidupkan
        statusLED = LOW;
      }
    }
    // delay(500);  // waktu jeda
  }  
  statusTombolAkhir = statusTombol;  // simpan status Tombol untuk loop1 selanjutnya
}
