# Fritzing sketch Skematik 2 LED + 2 TOMBOL (saved by Fritzing 0.9.2b)
breadboards: 1

parts:
  Part1 = Arduino Uno (Rev3)
  LED1 = LED - 5mm [color="Red (633nm)" package="5 mm [THT]"]
  S1 = Pushbutton [package="[SMD]"]
  R2 = Resistor [tolerance=±5% resistance=1k package="0805 [SMD]"]
  R1 = Resistor [tolerance=±5% resistance=220 package="0805 [SMD]"]
  LED2 = LED - 5mm [color="Red (633nm)" package="5 mm [THT]"]
  R3 = Resistor [tolerance=±5% resistance=220 package="0805 [SMD]"]  # not connected
  S2 = Pushbutton [package="[SMD]"]
  R4 = Resistor [tolerance=±5% resistance=1k package="0805 [SMD]"]

nets:
  N1: Part1.D8, R1.Pin_1
  N2: Part1.D2, Part1.D3_PWM, Part1.GND, LED1.cathode, S1.Pin_1, S1.Pin_2, R2.Pin_0, R2.Pin_1, LED2.cathode, S2.Pin_1, S2.Pin_2, R4.Pin_0, R4.Pin_1
  N3: Part1.5V, S1.Pin_3, S1.Pin_4, S2.Pin_3, S2.Pin_4
  N4: LED1.anode, R1.Pin_0

notes:
  Resistor 220Ω untuk Lampu LED
  Resistor 1kΩ untuk Tombol Push

// code stored in the sketch: 1Led1Saklar(1).ino
const int pinLED1 = 8; //  nomor pin LED 1
const int pinLED2 = 9; //  nomor pin LED 2
const int pinTombol1 = 2; // nomor pin Tombol 1
const int pinTombol2 = 3; // nomor pin Tombol 2


bool statusAkhirTombol1 = LOW;  // status Tombol 1 terakhir 
bool statusAkhirTombol2 = LOW;  // status Tombol 2 terakhir
bool statusLED1 = LOW;         // status LED 1
bool statusLED2 = LOW;         // status LED 2


void setup() {
  pinMode(pinLED1, OUTPUT);    // LED 1 sebagai output
  pinMode(pinLED2, OUTPUT);    // LED 2 sebagai output
  pinMode(pinTombol1, INPUT);  // Tombol 1 sebagai input
  pinMode(pinTombol2, INPUT);  // Tombol 2 sebagai input
}


void loop() {
  // LED 1
  bool statusTombol1 = digitalRead(pinTombol1);  // cek status Tombol
  if (statusTombol1 != statusAkhirTombol1) {       // jika status Tombol berubah dari sebelumnya
    if (statusTombol1 == HIGH) {                  // jika Tombol berubah ke status LOW (dilepas)
      if (statusLED1 == LOW) {          // jika status LED hidup
        digitalWrite(pinLED1, HIGH); // maka LED dimatikan
        statusLED1 = HIGH;
      } else {                        // jika status LED mati
        digitalWrite(pinLED1, LOW);  // maka LED dihidupkan
        statusLED1 = LOW;
      }
    }
    // delay(500);  // waktu jeda
  }  
  statusAkhirTombol1 = statusTombol1;  // simpan status Tombol untuk loop1 selanjutnya


  //LED 2
  bool statusTombol2 = digitalRead(pinTombol2);  // cek status Tombol
  if (statusTombol2 != statusAkhirTombol2) {       // jika status Tombol berubah dari sebelumnya
    if (statusTombol2 == HIGH) {                  // jika Tombol berubah ke status LOW (dilepas)
      if (statusLED2 == LOW) {          // jika status LED hidup
        digitalWrite(pinLED2, HIGH); // maka LED dimatikan
        statusLED2 = HIGH;
      } else {                        // jika status LED mati
        digitalWrite(pinLED2, LOW);  // maka LED dihidupkan
        statusLED2 = LOW;
      }
    }
    // delay(500);  // waktu jeda
  }  
  statusAkhirTombol2 = statusTombol2;  // simpan status Tombol untuk loop1 selanjutnya
}

// code stored in the sketch: 2Led2Saklar(1).ino
const int pinLED1 = 8; //  nomor pin LED 1
const int pinLED2 = 9; //  nomor pin LED 2
const int pinTombol1 = 2; // nomor pin Tombol 1
const int pinTombol2 = 3; // nomor pin Tombol 2


bool statusAkhirTombol1 = LOW;  // status Tombol 1 terakhir 
bool statusAkhirTombol2 = LOW;  // status Tombol 2 terakhir
bool statusLED1 = LOW;         // status LED 1
bool statusLED2 = LOW;         // status LED 2


void setup() {
  pinMode(pinLED1, OUTPUT);    // LED 1 sebagai output
  pinMode(pinLED2, OUTPUT);    // LED 2 sebagai output
  pinMode(pinTombol1, INPUT);  // Tombol 1 sebagai input
  pinMode(pinTombol2, INPUT);  // Tombol 2 sebagai input
}


void loop() {
  // LED 1
  bool statusTombol1 = digitalRead(pinTombol1);  // cek status Tombol
  if (statusTombol1 != statusAkhirTombol1) {       // jika status Tombol berubah dari sebelumnya
    if (statusTombol1 == HIGH) {                  // jika Tombol berubah ke status LOW (dilepas)
      if (statusLED1 == LOW) {          // jika status LED hidup
        digitalWrite(pinLED1, HIGH); // maka LED dimatikan
        statusLED1 = HIGH;
      } else {                        // jika status LED mati
        digitalWrite(pinLED1, LOW);  // maka LED dihidupkan
        statusLED1 = LOW;
      }
    }
    // delay(500);  // waktu jeda
  }  
  statusAkhirTombol1 = statusTombol1;  // simpan status Tombol untuk loop1 selanjutnya


  //LED 2
  bool statusTombol2 = digitalRead(pinTombol2);  // cek status Tombol
  if (statusTombol2 != statusAkhirTombol2) {       // jika status Tombol berubah dari sebelumnya
    if (statusTombol2 == HIGH) {                  // jika Tombol berubah ke status LOW (dilepas)
      if (statusLED2 == LOW) {          // jika status LED hidup
        digitalWrite(pinLED2, HIGH); // maka LED dimatikan
        statusLED2 = HIGH;
      } else {                        // jika status LED mati
        digitalWrite(pinLED2, LOW);  // maka LED dihidupkan
        statusLED2 = LOW;
      }
    }
    // delay(500);  // waktu jeda
  }  
  statusAkhirTombol2 = statusTombol2;  // simpan status Tombol untuk loop1 selanjutnya
}
